// Logisim project Circuit.circ as structural Verilog
module eightbit2compliment (
  input  I7,
  input  I6,
  input  I5,
  input  I4,
  input  I3,
  input  I2,
  input  I1,
  input  I0,
  output O6,
  output O5,
  output O4,
  output O3,
  output O2,
  output O1,
  output O0,
  output O7
);

  wire adder_2_cout, adder_3_cout, adder_4_cout, adder_5_cout, adder_6_cout, adder_7_cout, adder_8_cout,
       not_1_out, not_2_out, not_3_out, not_4_out, not_5_out, not_6_out, not_7_out, not_8_out;

  not not_1 (not_1_out, I7);
  not not_2 (not_2_out, I6);
  Adder #(.width(1)) adder_1 (.a(not_1_out), .b(adder_2_cout), .out(O7));  // open: cin, cout
  not not_3 (not_3_out, I5);
  Adder #(.width(1)) adder_2 (.a(not_2_out), .b(adder_3_cout), .out(O6), .cout(adder_2_cout));  // open: cin
  not not_4 (not_4_out, I4);
  Adder #(.width(1)) adder_3 (.a(not_3_out), .b(adder_4_cout), .out(O5), .cout(adder_3_cout));  // open: cin
  not not_5 (not_5_out, I3);
  Adder #(.width(1)) adder_4 (.a(not_4_out), .b(adder_5_cout), .out(O4), .cout(adder_4_cout));  // open: cin
  not not_6 (not_6_out, I2);
  Adder #(.width(1)) adder_5 (.a(not_5_out), .b(adder_6_cout), .out(O3), .cout(adder_5_cout));  // open: cin
  not not_7 (not_7_out, I1);
  Adder #(.width(1)) adder_6 (.a(not_6_out), .b(adder_7_cout), .out(O2), .cout(adder_6_cout));  // open: cin
  not not_8 (not_8_out, I0);
  Adder #(.width(1)) adder_7 (.a(not_7_out), .b(adder_8_cout), .out(O1), .cout(adder_7_cout));  // open: cin
  Adder #(.width(1)) adder_8 (.a(not_8_out), .b(1'b1), .out(O0), .cout(adder_8_cout));  // open: cin
endmodule

// reg
module shiftRightReg (
  input  i_0,
  input  i_1,
  input  i_2,
  input  i_3,
  input  i_4,
  input  i_5,
  input  i_6,
  input  i_7,
  input  Clock,
  input  Enable,
  input  Load,
  output out_12
);

  wire d_ff_1_q, d_ff_3_q, d_ff_4_q, d_ff_5_q, d_ff_6_q, d_ff_7_q, d_ff_8_q, multiplexer_1_out,
       multiplexer_2_out, multiplexer_3_out, multiplexer_4_out, multiplexer_5_out, multiplexer_6_out,
       multiplexer_7_out, multiplexer_8_out, multiplexer_9_out, multiplexer_10_out, multiplexer_11_out,
       multiplexer_12_out, multiplexer_13_out, multiplexer_14_out, multiplexer_15_out, multiplexer_16_out,
       undriven, undriven_2, undriven_3, undriven_4, undriven_5, undriven_6, undriven_7, undriven_8;

  Multiplexer multiplexer_1 (.in0(1'b0), .in1(i_0), .out(multiplexer_1_out), .sel(Load));
  D_Flip_Flop d_ff_1 (.D(multiplexer_2_out), .clk(Clock), .Q(d_ff_1_q), .reset(undriven));  // open: Qn, preset
  Multiplexer multiplexer_2 (.in0(d_ff_1_q), .in1(multiplexer_1_out), .out(multiplexer_2_out), .sel(Enable));
  D_Flip_Flop d_ff_2 ();  // open: D, clk, Q, Qn, preset, reset
  Multiplexer multiplexer_3 (.in0(d_ff_1_q), .in1(i_1), .out(multiplexer_3_out), .sel(Load));
  D_Flip_Flop d_ff_3 (.D(multiplexer_4_out), .clk(Clock), .Q(d_ff_3_q), .reset(undriven_2));  // open: Qn, preset
  Multiplexer multiplexer_4 (.in0(d_ff_3_q), .in1(multiplexer_3_out), .out(multiplexer_4_out), .sel(Enable));
  Multiplexer multiplexer_5 (.in0(d_ff_4_q), .in1(multiplexer_6_out), .out(multiplexer_5_out), .sel(Enable));
  Multiplexer multiplexer_6 (.in0(d_ff_3_q), .in1(i_2), .out(multiplexer_6_out), .sel(Load));
  D_Flip_Flop d_ff_4 (.D(multiplexer_5_out), .clk(Clock), .Q(d_ff_4_q), .reset(undriven_3));  // open: Qn, preset
  Multiplexer multiplexer_7 (.in0(d_ff_4_q), .in1(i_3), .out(multiplexer_7_out), .sel(Load));
  D_Flip_Flop d_ff_5 (.D(multiplexer_8_out), .clk(Clock), .Q(d_ff_5_q), .reset(undriven_4));  // open: Qn, preset
  Multiplexer multiplexer_8 (.in0(d_ff_5_q), .in1(multiplexer_7_out), .out(multiplexer_8_out), .sel(Enable));
  Multiplexer multiplexer_9 (.in0(d_ff_5_q), .in1(i_4), .out(multiplexer_9_out), .sel(Load));
  Multiplexer multiplexer_10 (.in0(d_ff_6_q), .in1(multiplexer_9_out), .out(multiplexer_10_out), .sel(Enable));
  D_Flip_Flop d_ff_6 (.D(multiplexer_10_out), .clk(Clock), .Q(d_ff_6_q), .reset(undriven_5));  // open: Qn, preset
  Multiplexer multiplexer_11 (.in0(d_ff_6_q), .in1(i_5), .out(multiplexer_11_out), .sel(Load));
  Multiplexer multiplexer_12 (.in0(d_ff_7_q), .in1(multiplexer_11_out), .out(multiplexer_12_out), .sel(Enable));
  D_Flip_Flop d_ff_7 (.D(multiplexer_12_out), .clk(Clock), .Q(d_ff_7_q), .reset(undriven_6));  // open: Qn, preset
  Multiplexer multiplexer_13 (.in0(d_ff_7_q), .in1(i_6), .out(multiplexer_13_out), .sel(Load));
  Multiplexer multiplexer_14 (.in0(d_ff_8_q), .in1(multiplexer_13_out), .out(multiplexer_14_out), .sel(Enable));
  D_Flip_Flop d_ff_8 (.D(multiplexer_14_out), .clk(Clock), .Q(d_ff_8_q), .reset(undriven_7));  // open: Qn, preset
  Multiplexer multiplexer_15 (.in0(d_ff_8_q), .in1(i_7), .out(multiplexer_15_out), .sel(Load));
  Multiplexer multiplexer_16 (.in0(out_12), .in1(multiplexer_15_out), .out(multiplexer_16_out), .sel(Enable));
  D_Flip_Flop d_ff_9 (.D(multiplexer_16_out), .clk(Clock), .Q(out_12), .reset(undriven_8));  // open: Qn, preset
endmodule

module shiftLeftReg (
  input  i_0,
  input  i_1,
  input  i_2,
  input  i_3,
  input  i_4,
  input  i_5,
  input  i_6,
  input  i_7,
  input  Clock,
  input  Enable,
  input  Load,
  output out_12
);

  wire d_ff_2_q, d_ff_3_q, d_ff_4_q, d_ff_5_q, d_ff_6_q, d_ff_7_q, d_ff_8_q, multiplexer_1_out,
       multiplexer_2_out, multiplexer_3_out, multiplexer_4_out, multiplexer_5_out, multiplexer_6_out,
       multiplexer_7_out, multiplexer_8_out, multiplexer_9_out, multiplexer_10_out, multiplexer_11_out,
       multiplexer_12_out, multiplexer_13_out, multiplexer_14_out, multiplexer_15_out, multiplexer_16_out,
       undriven, undriven_2, undriven_3, undriven_4, undriven_5, undriven_6, undriven_7, undriven_8;

  Multiplexer multiplexer_1 (.in0(d_ff_2_q), .in1(i_0), .out(multiplexer_1_out), .sel(Load));
  D_Flip_Flop d_ff_1 (.D(multiplexer_2_out), .clk(Clock), .Q(out_12), .reset(undriven));  // open: Qn, preset
  Multiplexer multiplexer_2 (.in0(out_12), .in1(multiplexer_1_out), .out(multiplexer_2_out), .sel(Enable));
  LED led_1 (.in(out_12));
  Multiplexer multiplexer_3 (.in0(d_ff_3_q), .in1(i_1), .out(multiplexer_3_out), .sel(Load));
  D_Flip_Flop d_ff_2 (.D(multiplexer_4_out), .clk(Clock), .Q(d_ff_2_q), .reset(undriven_2));  // open: Qn, preset
  Multiplexer multiplexer_4 (.in0(d_ff_2_q), .in1(multiplexer_3_out), .out(multiplexer_4_out), .sel(Enable));
  Multiplexer multiplexer_5 (.in0(d_ff_3_q), .in1(multiplexer_6_out), .out(multiplexer_5_out), .sel(Enable));
  Multiplexer multiplexer_6 (.in0(d_ff_4_q), .in1(i_2), .out(multiplexer_6_out), .sel(Load));
  D_Flip_Flop d_ff_3 (.D(multiplexer_5_out), .clk(Clock), .Q(d_ff_3_q), .reset(undriven_3));  // open: Qn, preset
  Multiplexer multiplexer_7 (.in0(d_ff_5_q), .in1(i_3), .out(multiplexer_7_out), .sel(Load));
  D_Flip_Flop d_ff_4 (.D(multiplexer_8_out), .clk(Clock), .Q(d_ff_4_q), .reset(undriven_4));  // open: Qn, preset
  Multiplexer multiplexer_8 (.in0(d_ff_4_q), .in1(multiplexer_7_out), .out(multiplexer_8_out), .sel(Enable));
  Multiplexer multiplexer_9 (.in0(d_ff_6_q), .in1(i_4), .out(multiplexer_9_out), .sel(Load));
  Multiplexer multiplexer_10 (.in0(d_ff_5_q), .in1(multiplexer_9_out), .out(multiplexer_10_out), .sel(Enable));
  D_Flip_Flop d_ff_5 (.D(multiplexer_10_out), .clk(Clock), .Q(d_ff_5_q), .reset(undriven_5));  // open: Qn, preset
  Multiplexer multiplexer_11 (.in0(d_ff_7_q), .in1(i_5), .out(multiplexer_11_out), .sel(Load));
  Multiplexer multiplexer_12 (.in0(d_ff_6_q), .in1(multiplexer_11_out), .out(multiplexer_12_out), .sel(Enable));
  D_Flip_Flop d_ff_6 (.D(multiplexer_12_out), .clk(Clock), .Q(d_ff_6_q), .reset(undriven_6));  // open: Qn, preset
  Multiplexer multiplexer_13 (.in0(d_ff_8_q), .in1(i_6), .out(multiplexer_13_out), .sel(Load));
  Multiplexer multiplexer_14 (.in0(d_ff_7_q), .in1(multiplexer_13_out), .out(multiplexer_14_out), .sel(Enable));
  D_Flip_Flop d_ff_7 (.D(multiplexer_14_out), .clk(Clock), .Q(d_ff_7_q), .reset(undriven_7));  // open: Qn, preset
  Multiplexer multiplexer_15 (.in0(1'b0), .in1(i_7), .out(multiplexer_15_out), .sel(Load));
  Multiplexer multiplexer_16 (.in0(d_ff_8_q), .in1(multiplexer_15_out), .out(multiplexer_16_out), .sel(Enable));
  D_Flip_Flop d_ff_8 (.D(multiplexer_16_out), .clk(Clock), .Q(d_ff_8_q), .reset(undriven_8));  // open: Qn, preset
endmodule

module ControlUnit (
  input  B0,
  input  Z,
  input  Load,
  output Psel,
  output EP,
  output EA,
  output EB,
  output LA,
  output LB,
  output RstP
);

  wire not_2_out;

  not not_1 (EA, Z);
  not not_2 (not_2_out, Load);
  and and_1 (EP, not_2_out, EA);

  assign EB = EA;
  assign LA = Load;
  assign LB = Load;
  assign Psel = B0;
  assign RstP = Load;
endmodule

module PReg (
  input  I_0,
  input  Clock,
  input  Reset,
  input  Load,
  input  I_1,
  input  I_2,
  input  I_3,
  input  I_4,
  input  I_5,
  input  I_6,
  input  I_7,
  input  I_8,
  input  I_9,
  input  I_10,
  input  I_11,
  input  I_12,
  input  I_13,
  input  I_14,
  input  I_15,
  output Out_0,
  output Out_1,
  output Out_2,
  output Out_3,
  output Out_4,
  output Out_5,
  output Out_6,
  output Out_7,
  output Out_8,
  output Out_9,
  output Out_10,
  output Out_11,
  output Out_12,
  output Out_13,
  output Out_14,
  output Out_15
);

  wire multiplexer_1_out, multiplexer_2_out, multiplexer_3_out, multiplexer_4_out, multiplexer_5_out,
       multiplexer_6_out, multiplexer_7_out, multiplexer_8_out, multiplexer_9_out, multiplexer_10_out,
       multiplexer_11_out, multiplexer_12_out, multiplexer_13_out, multiplexer_14_out, multiplexer_15_out,
       multiplexer_16_out;

  Multiplexer multiplexer_1 (.in0(Out_2), .in1(I_2), .out(multiplexer_1_out), .sel(Load));
  Multiplexer multiplexer_2 (.in0(Out_3), .in1(I_3), .out(multiplexer_2_out), .sel(Load));
  Multiplexer multiplexer_3 (.in0(Out_4), .in1(I_4), .out(multiplexer_3_out), .sel(Load));
  Multiplexer multiplexer_4 (.in0(Out_5), .in1(I_5), .out(multiplexer_4_out), .sel(Load));
  Multiplexer multiplexer_5 (.in0(Out_6), .in1(I_6), .out(multiplexer_5_out), .sel(Load));
  Multiplexer multiplexer_6 (.in0(Out_7), .in1(I_7), .out(multiplexer_6_out), .sel(Load));
  Multiplexer multiplexer_7 (.in0(Out_8), .in1(I_8), .out(multiplexer_7_out), .sel(Load));
  Multiplexer multiplexer_8 (.in0(Out_9), .in1(I_9), .out(multiplexer_8_out), .sel(Load));
  Multiplexer multiplexer_9 (.in0(Out_10), .in1(I_10), .out(multiplexer_9_out), .sel(Load));
  Multiplexer multiplexer_10 (.in0(Out_11), .in1(I_11), .out(multiplexer_10_out), .sel(Load));
  Multiplexer multiplexer_11 (.in0(Out_12), .in1(I_12), .out(multiplexer_11_out), .sel(Load));
  Multiplexer multiplexer_12 (.in0(Out_13), .in1(I_13), .out(multiplexer_12_out), .sel(Load));
  Multiplexer multiplexer_13 (.in0(Out_14), .in1(I_14), .out(multiplexer_13_out), .sel(Load));
  Multiplexer multiplexer_14 (.in0(Out_15), .in1(I_15), .out(multiplexer_14_out), .sel(Load));
  Multiplexer multiplexer_15 (.in0(Out_0), .in1(I_0), .out(multiplexer_15_out), .sel(Load));
  D_Flip_Flop d_ff_1 (.D(multiplexer_15_out), .clk(Clock), .Q(Out_0), .reset(Reset));  // open: Qn, preset
  Multiplexer multiplexer_16 (.in0(Out_1), .in1(I_1), .out(multiplexer_16_out), .sel(Load));
  D_Flip_Flop d_ff_2 (.D(multiplexer_16_out), .clk(Clock), .Q(Out_1), .reset(Reset));  // open: Qn, preset
  D_Flip_Flop d_ff_3 (.D(multiplexer_1_out), .clk(Clock), .Q(Out_2), .reset(Reset));  // open: Qn, preset
  D_Flip_Flop d_ff_4 (.D(multiplexer_2_out), .clk(Clock), .Q(Out_3), .reset(Reset));  // open: Qn, preset
  D_Flip_Flop d_ff_5 (.D(multiplexer_3_out), .clk(Clock), .Q(Out_4), .reset(Reset));  // open: Qn, preset
  D_Flip_Flop d_ff_6 (.D(multiplexer_4_out), .clk(Clock), .Q(Out_5), .reset(Reset));  // open: Qn, preset
  D_Flip_Flop d_ff_7 (.D(multiplexer_5_out), .clk(Clock), .Q(Out_6), .reset(Reset));  // open: Qn, preset
  D_Flip_Flop d_ff_8 (.D(multiplexer_6_out), .clk(Clock), .Q(Out_7), .reset(Reset));  // open: Qn, preset
  D_Flip_Flop d_ff_9 (.D(multiplexer_7_out), .clk(Clock), .Q(Out_8), .reset(Reset));  // open: Qn, preset
  D_Flip_Flop d_ff_10 (.D(multiplexer_8_out), .clk(Clock), .Q(Out_9), .reset(Reset));  // open: Qn, preset
  D_Flip_Flop d_ff_11 (.D(multiplexer_9_out), .clk(Clock), .Q(Out_10), .reset(Reset));  // open: Qn, preset
  D_Flip_Flop d_ff_12 (.D(multiplexer_10_out), .clk(Clock), .Q(Out_11), .reset(Reset));  // open: Qn, preset
  D_Flip_Flop d_ff_13 (.D(multiplexer_11_out), .clk(Clock), .Q(Out_12), .reset(Reset));  // open: Qn, preset
  D_Flip_Flop d_ff_14 (.D(multiplexer_12_out), .clk(Clock), .Q(Out_13), .reset(Reset));  // open: Qn, preset
  D_Flip_Flop d_ff_15 (.D(multiplexer_13_out), .clk(Clock), .Q(Out_14), .reset(Reset));  // open: Qn, preset
  D_Flip_Flop d_ff_16 (.D(multiplexer_14_out), .clk(Clock), .Q(Out_15), .reset(Reset));  // open: Qn, preset
endmodule
